# Fritzing sketch Board (saved by Fritzing 0.9.3b)
breadboards: 1

parts:
  Bauteil1 = Arduino Uno (Rev3)
  NEOPIXEL1 = Neopixel Strip -- Black (30/m)
  PIR1 = PIR sensor
  J1 = Basic Servo
  J2 = Piezo Speaker
  R1 = Resistor [tolerance=±5% resistance=100 package=THT]

nets:
  N1: Bauteil1.D8, R1.Pin_0
  N2: Bauteil1.D9_PWM, PIR1.SIG
  N3: Bauteil1.D10_PWM/SS, J1.pulse
  N4: Bauteil1.D11_PWM/MOSI, NEOPIXEL1.Din
  5V: Bauteil1.5V, NEOPIXEL1.+5V, PIR1.VDD, J1.vcc
  GND: Bauteil1.GND, NEOPIXEL1.GND, PIR1.GND, J1.gnd, J2.pin1
  N5: J2.pin2, R1.Pin_1

custom parts:
  Neopixel Strip -- Black (30/m): These NeoPixel strips have 30 digitally-addressable pixel LEDs per meter and are very affordable and are only 12.5 mm wide, 10 mm if you remove the strip from the casing.
